// Logisim project CRC.circ as structural Verilog: 2 circuits, main circuit CRC
module CRC (
  input  [7:0] A,
  input  [3:0] B,
  output [10:0] out_3
);

  wire [2:0] mod2_1_c, mod2_2_c, mod2_3_c, mod2_4_c, mod2_5_c, mod2_7_c;
  wire [3:1] mod2_6_c;

  mod2 mod2_1 (.A(A[7:4]), .B(B), .C(mod2_1_c));
  mod2 mod2_2 (.A({mod2_1_c, A[3]}), .B(B), .C(mod2_2_c));
  mod2 mod2_3 (.A({mod2_2_c, A[2]}), .B(B), .C(mod2_3_c));
  mod2 mod2_4 (.A({mod2_3_c, A[1]}), .B(B), .C(mod2_4_c));
  mod2 mod2_5 (.A({mod2_4_c, A[0]}), .B(B), .C(mod2_5_c));
  mod2 mod2_6 (.A({mod2_5_c, 1'b0}), .B(B), .C(mod2_6_c));
  mod2 mod2_7 (.A({mod2_6_c, 1'b0}), .B(B), .C(mod2_7_c));
  mod2 mod2_8 (.A({mod2_7_c, 1'b0}), .B(B), .C(out_3[2:0]));

  assign out_3[10:3] = A;
endmodule

module mod2 (
  input  [3:0] A,
  input  [3:0] B,
  output [2:0] C
);

  wire [3:0] multiplexer_1_out;

  Multiplexer #(.width(4)) multiplexer_1 (.in0(4'b0000), .in1(B), .out(multiplexer_1_out), .sel(A[3]));  // open: en
  xor xor_1 (C[0], A[0], multiplexer_1_out[0]);
  xor xor_2 (C[1], A[1], multiplexer_1_out[1]);
  xor xor_3 (C[2], A[2], multiplexer_1_out[2]);

  // Other names for the same wires on the sheet: D = A[3]
endmodule
