// Logisim project GRF.circ as structural Verilog: 2 circuits, main circuit grf
module grf (
  input  [31:0] WD,
  input  [4:0] A3,
  input  [4:0] A1,
  input  WE,
  input  reset,
  input  clk,
  input  [4:0] A2,
  output [31:0] RD1,
  output [31:0] RD2
);

  wire [31:0] _0, _1, _2, _3, _4, _5, _6, _7, _8, _9, _10, _11, _12, _13, _14, _15, _16, _17, _18, _19, _20,
       _21, _22, _23, _24, _25, _26, _27, _28, _29, _30, _31, demultiplexer_1_out1, demultiplexer_1_out2,
       demultiplexer_1_out3, demultiplexer_1_out4, demultiplexer_1_out5, demultiplexer_1_out6,
       demultiplexer_1_out7, demultiplexer_1_out8, demultiplexer_1_out9, demultiplexer_1_out10,
       demultiplexer_1_out11, demultiplexer_1_out12, demultiplexer_1_out13, demultiplexer_1_out14,
       demultiplexer_1_out15, demultiplexer_1_out16, demultiplexer_1_out17, demultiplexer_1_out18,
       demultiplexer_1_out19, demultiplexer_1_out20, demultiplexer_1_out21, demultiplexer_1_out22,
       demultiplexer_1_out23, demultiplexer_1_out24, demultiplexer_1_out25, demultiplexer_1_out26,
       demultiplexer_1_out27, demultiplexer_1_out28, demultiplexer_1_out29, demultiplexer_1_out30,
       demultiplexer_1_out31;

  Demultiplexer #(.select(5), .width(32), .tristate("true")) demultiplexer_1 (
    .out1(demultiplexer_1_out1), .out2(demultiplexer_1_out2), .out3(demultiplexer_1_out3),
    .out4(demultiplexer_1_out4), .out5(demultiplexer_1_out5), .out6(demultiplexer_1_out6),
    .out7(demultiplexer_1_out7), .out8(demultiplexer_1_out8), .out9(demultiplexer_1_out9),
    .out10(demultiplexer_1_out10), .out11(demultiplexer_1_out11), .out12(demultiplexer_1_out12),
    .out13(demultiplexer_1_out13), .out14(demultiplexer_1_out14), .out15(demultiplexer_1_out15),
    .out16(demultiplexer_1_out16), .out17(demultiplexer_1_out17), .out18(demultiplexer_1_out18),
    .out19(demultiplexer_1_out19), .out20(demultiplexer_1_out20), .out21(demultiplexer_1_out21),
    .out22(demultiplexer_1_out22), .out23(demultiplexer_1_out23), .out24(demultiplexer_1_out24),
    .out25(demultiplexer_1_out25), .out26(demultiplexer_1_out26), .out27(demultiplexer_1_out27),
    .out28(demultiplexer_1_out28), .out29(demultiplexer_1_out29), .out30(demultiplexer_1_out30),
    .out31(demultiplexer_1_out31), .in(WD), .sel(A3), .en(WE));  // open: out0
  \reg  \reg  (
    ._1(demultiplexer_1_out1), .in_5(demultiplexer_1_out2), .in_6(demultiplexer_1_out3),
    .in_7(demultiplexer_1_out4), .in_8(demultiplexer_1_out5), .in_9(demultiplexer_1_out6),
    .in_10(demultiplexer_1_out7), .in_11(demultiplexer_1_out8), .in_12(demultiplexer_1_out9),
    .in_13(demultiplexer_1_out10), .in_14(demultiplexer_1_out11), .in_15(demultiplexer_1_out12),
    .in_16(demultiplexer_1_out13), .in_17(demultiplexer_1_out14), .in_18(demultiplexer_1_out15),
    .in_19(demultiplexer_1_out16), .in_20(demultiplexer_1_out17), .in_21(demultiplexer_1_out18),
    .in_22(demultiplexer_1_out19), .in_23(demultiplexer_1_out20), .in_24(demultiplexer_1_out21),
    .in_25(demultiplexer_1_out22), .in_26(demultiplexer_1_out23), .in_27(demultiplexer_1_out24),
    .in_28(demultiplexer_1_out25), .in_29(demultiplexer_1_out26), .in_30(demultiplexer_1_out27),
    .in_31(demultiplexer_1_out28), .in_32(demultiplexer_1_out29), .in_33(demultiplexer_1_out30),
    ._31(demultiplexer_1_out31), .WE(WE), .reset(reset), .clk(clk), ._0(_0), ._1_2(_1), ._2(_2), ._3(_3),
    ._4(_4), ._5(_5), ._6(_6), ._7(_7), ._8(_8), ._9(_9), .out_45(_10), .out_46(_11), .out_47(_12),
    .out_48(_13), .out_49(_14), .out_50(_15), .out_51(_16), .out_52(_17), .out_53(_18), .out_54(_19),
    .out_55(_20), .out_56(_21), .out_57(_22), .out_58(_23), .out_59(_24), .out_60(_25), .out_61(_26),
    .out_62(_27), .out_63(_28), .out_64(_29), .out_65(_30), ._31_2(_31));
  Multiplexer #(.select(5), .width(32)) multiplexer_1 (
    .in0(_0), .in1(_1), .in2(_2), .in3(_3), .in4(_4), .in5(_5), .in6(_6), .in7(_7), .in8(_8), .in9(_9),
    .in10(_10), .in11(_11), .in12(_12), .in13(_13), .in14(_14), .in15(_15), .in16(_16), .in17(_17),
    .in18(_18), .in19(_19), .in20(_20), .in21(_21), .in22(_22), .in23(_23), .in24(_24), .in25(_25),
    .in26(_26), .in27(_27), .in28(_28), .in29(_29), .in30(_30), .in31(_31), .out(RD1), .sel(A1));  // open: en
  Multiplexer #(.select(5), .width(32)) multiplexer_2 (
    .in0(_0), .in1(_1), .in2(_2), .in3(_3), .in4(_4), .in5(_5), .in6(_6), .in7(_7), .in8(_8), .in9(_9),
    .in10(_10), .in11(_11), .in12(_12), .in13(_13), .in14(_14), .in15(_15), .in16(_16), .in17(_17),
    .in18(_18), .in19(_19), .in20(_20), .in21(_21), .in22(_22), .in23(_23), .in24(_24), .in25(_25),
    .in26(_26), .in27(_27), .in28(_28), .in29(_29), .in30(_30), .in31(_31), .out(RD2), .sel(A2));  // open: en
endmodule

module \reg  (
  input  WE,
  input  reset,
  input  clk,
  input  [31:0] _1,
  input  [31:0] in_5,
  input  [31:0] in_6,
  input  [31:0] in_7,
  input  [31:0] in_8,
  input  [31:0] in_9,
  input  [31:0] in_10,
  input  [31:0] in_11,
  input  [31:0] in_12,
  input  [31:0] in_13,
  input  [31:0] in_14,
  input  [31:0] in_15,
  input  [31:0] in_16,
  input  [31:0] in_17,
  input  [31:0] in_18,
  input  [31:0] in_19,
  input  [31:0] in_20,
  input  [31:0] in_21,
  input  [31:0] in_22,
  input  [31:0] in_23,
  input  [31:0] in_24,
  input  [31:0] in_25,
  input  [31:0] in_26,
  input  [31:0] in_27,
  input  [31:0] in_28,
  input  [31:0] in_29,
  input  [31:0] in_30,
  input  [31:0] in_31,
  input  [31:0] in_32,
  input  [31:0] in_33,
  input  [31:0] _31,
  output [31:0] _0,
  output [31:0] _1_2,
  output [31:0] _2,
  output [31:0] _3,
  output [31:0] _4,
  output [31:0] _5,
  output [31:0] _6,
  output [31:0] _7,
  output [31:0] _8,
  output [31:0] _9,
  output [31:0] out_45,
  output [31:0] out_46,
  output [31:0] out_47,
  output [31:0] out_48,
  output [31:0] out_49,
  output [31:0] out_50,
  output [31:0] out_51,
  output [31:0] out_52,
  output [31:0] out_53,
  output [31:0] out_54,
  output [31:0] out_55,
  output [31:0] out_56,
  output [31:0] out_57,
  output [31:0] out_58,
  output [31:0] out_59,
  output [31:0] out_60,
  output [31:0] out_61,
  output [31:0] out_62,
  output [31:0] out_63,
  output [31:0] out_64,
  output [31:0] out_65,
  output [31:0] _31_2
);

  Register #(.width(32)) register_1 (.D({32{1'b0}}), .en(WE), .Q(_0), .clk(clk), .clr(reset));
  Register #(.width(32)) register_2 (.D(in_11), .en(WE), .Q(_8), .clk(clk), .clr(reset));
  Register #(.width(32)) register_3 (.D(in_19), .en(WE), .Q(out_51), .clk(clk), .clr(reset));
  Register #(.width(32)) register_4 (.D(in_27), .en(WE), .Q(out_59), .clk(clk), .clr(reset));
  Register #(.width(32)) register_5 (.D(_1), .en(WE), .Q(_1_2), .clk(clk), .clr(reset));
  Register #(.width(32)) register_6 (.D(in_12), .en(WE), .Q(_9), .clk(clk), .clr(reset));
  Register #(.width(32)) register_7 (.D(in_20), .en(WE), .Q(out_52), .clk(clk), .clr(reset));
  Register #(.width(32)) register_8 (.D(in_28), .en(WE), .Q(out_60), .clk(clk), .clr(reset));
  Register #(.width(32)) register_9 (.D(in_5), .en(WE), .Q(_2), .clk(clk), .clr(reset));
  Register #(.width(32)) register_10 (.D(in_13), .en(WE), .Q(out_45), .clk(clk), .clr(reset));
  Register #(.width(32)) register_11 (.D(in_21), .en(WE), .Q(out_53), .clk(clk), .clr(reset));
  Register #(.width(32)) register_12 (.D(in_29), .en(WE), .Q(out_61), .clk(clk), .clr(reset));
  Register #(.width(32)) register_13 (.D(in_6), .en(WE), .Q(_3), .clk(clk), .clr(reset));
  Register #(.width(32)) register_14 (.D(in_14), .en(WE), .Q(out_46), .clk(clk), .clr(reset));
  Register #(.width(32)) register_15 (.D(in_22), .en(WE), .Q(out_54), .clk(clk), .clr(reset));
  Register #(.width(32)) register_16 (.D(in_30), .en(WE), .Q(out_62), .clk(clk), .clr(reset));
  Register #(.width(32)) register_17 (.D(in_7), .en(WE), .Q(_4), .clk(clk), .clr(reset));
  Register #(.width(32)) register_18 (.D(in_15), .en(WE), .Q(out_47), .clk(clk), .clr(reset));
  Register #(.width(32)) register_19 (.D(in_23), .en(WE), .Q(out_55), .clk(clk), .clr(reset));
  Register #(.width(32)) register_20 (.D(in_31), .en(WE), .Q(out_63), .clk(clk), .clr(reset));
  Register #(.width(32)) register_21 (.D(in_8), .en(WE), .Q(_5), .clk(clk), .clr(reset));
  Register #(.width(32)) register_22 (.D(in_16), .en(WE), .Q(out_48), .clk(clk), .clr(reset));
  Register #(.width(32)) register_23 (.D(in_24), .en(WE), .Q(out_56), .clk(clk), .clr(reset));
  Register #(.width(32)) register_24 (.D(in_32), .en(WE), .Q(out_64), .clk(clk), .clr(reset));
  Register #(.width(32)) register_25 (.D(in_9), .en(WE), .Q(_6), .clk(clk), .clr(reset));
  Register #(.width(32)) register_26 (.D(in_17), .en(WE), .Q(out_49), .clk(clk), .clr(reset));
  Register #(.width(32)) register_27 (.D(in_25), .en(WE), .Q(out_57), .clk(clk), .clr(reset));
  Register #(.width(32)) register_28 (.D(in_33), .en(WE), .Q(out_65), .clk(clk), .clr(reset));
  Register #(.width(32)) register_29 (.D(in_10), .en(WE), .Q(_7), .clk(clk), .clr(reset));
  Register #(.width(32)) register_30 (.D(in_18), .en(WE), .Q(out_50), .clk(clk), .clr(reset));
  Register #(.width(32)) register_31 (.D(in_26), .en(WE), .Q(out_58), .clk(clk), .clr(reset));
  Register #(.width(32)) register_32 (.D(_31), .en(WE), .Q(_31_2), .clk(clk), .clr(reset));

  // Other names for the same wires on the sheet: _1_t[31:0] = _1_2; _10[31:0] = out_45; _11[31:0] = out_46;
  //   _12[31:0] = out_47; _13[31:0] = out_48; _14[31:0] = out_49; _15[31:0] = out_50; _16[31:0] = out_51;
  //   _17[31:0] = out_52; _18[31:0] = out_53; _19[31:0] = out_54; _20[31:0] = out_55; _21[31:0] = out_56;
  //   _22[31:0] = out_57; _23[31:0] = out_58; _24[31:0] = out_59; _25[31:0] = out_60; _26[31:0] = out_61;
  //   _27[31:0] = out_62; _28[31:0] = out_63; _29[31:0] = out_64; _30[31:0] = out_65; _31_t[31:0] = _31_2;
  //   I1[31:0] = _1; I2[31:0] = in_5; I3[31:0] = in_6; I4[31:0] = in_7; I5[31:0] = in_8; I6[31:0] = in_9;
  //   I7[31:0] = in_10; I8[31:0] = in_11; I9[31:0] = in_12; I10[31:0] = in_13; I11[31:0] = in_14; I12[31:0] = in_15;
  //   I13[31:0] = in_16; I14[31:0] = in_17; I15[31:0] = in_18; I16[31:0] = in_19; I17[31:0] = in_20;
  //   I18[31:0] = in_21; I19[31:0] = in_22; I20[31:0] = in_23; I21[31:0] = in_24; I22[31:0] = in_25;
  //   I23[31:0] = in_26; I24[31:0] = in_27; I25[31:0] = in_28; I26[31:0] = in_29; I27[31:0] = in_30;
  //   I28[31:0] = in_31; I29[31:0] = in_32; I30[31:0] = in_33; I31[31:0] = _31
endmodule
