// Logisim project ct74151.circ as structural Verilog: 1 circuit, main circuit main
module main (
  input  D0,
  input  D0_2,
  input  D0_3,
  input  D0_4,
  input  D1,
  input  D1_2,
  input  D1_3,
  input  D1_4,
  input  D2,
  input  D2_2,
  input  D2_3,
  input  D2_4,
  input  D3,
  input  D3_2,
  input  D3_3,
  input  D3_4,
  input  D4,
  input  D4_2,
  input  D4_3,
  input  D4_4,
  input  D5,
  input  D5_2,
  input  D5_3,
  input  D5_4,
  input  D6,
  input  D6_2,
  input  D6_3,
  input  D6_4,
  input  D7,
  input  D7_2,
  input  D7_3,
  input  D7_4,
  input  A,
  input  B,
  input  C,
  input  D,
  input  E,
  output F_A_B_C_D_E
);

  wire and_1_out, and_2_out, and_3_out, and_4_out, not_1_out, not_2_out, not_3_out, not_4_out, O1, O2, O3, O4;

  not not_1 (not_1_out, E);
  not not_2 (not_2_out, D);
  not not_3 (not_3_out, E);
  not not_4 (not_4_out, D);
  Multiplexer #(.select(3)) multiplexer_1 (
    .in0(D0), .in1(D1), .in2(D2), .in3(D3), .in4(D4), .in5(D5), .in6(D6), .in7(D7), .out(O1), .sel({A, B, C}));  // open: en
  and and_1 (and_1_out, O1, D, E);
  and and_2 (and_2_out, O2, D, not_1_out);
  and and_3 (and_3_out, O3, not_2_out, D);
  and and_4 (and_4_out, O4, not_3_out, not_4_out);
  Multiplexer #(.select(3)) multiplexer_2 (
    .in0(D0_2), .in1(D1_2), .in2(D2_2), .in3(D3_2), .in4(D4_2), .in5(D5_2), .in6(D6_2), .in7(D7_2), .out(O2),
    .sel({A, B, C}));  // open: en
  or or_1 (F_A_B_C_D_E, and_1_out, and_2_out, and_3_out, and_4_out);
  Multiplexer #(.select(3)) multiplexer_3 (
    .in0(D0_3), .in1(D1_3), .in2(D2_3), .in3(D3_3), .in4(D4_3), .in5(D5_3), .in6(D6_3), .in7(D7_3), .out(O3),
    .sel({A, B, C}));  // open: en
  Multiplexer #(.select(3)) multiplexer_4 (
    .in0(D0_4), .in1(D1_4), .in2(D2_4), .in3(D3_4), .in4(D4_4), .in5(D5_4), .in6(D6_4), .in7(D7_4), .out(O4),
    .sel({A, B, C}));  // open: en
endmodule
