// Logisim project fib.circ as structural Verilog: 3 circuits, main circuit main
module main (
  input  [2:0] N,
  output [3:0] Nth
);

  wire count_1_out_2;
  wire [3:0] calculator_1_now_value;

  count count_1 (.\input (N), .out_2(count_1_out_2));
  calculator calculator_1 (.signal(count_1_out_2), .now_value(calculator_1_now_value));
  Multiplexer #(.width(4)) multiplexer_1 (
    .in0(4'b0000), .in1(calculator_1_now_value), .out(Nth), .sel(count_1_out_2));  // open: en
endmodule

module count (
  input  [2:0] \input ,
  output out_2
);

  wire clock_1_out;
  wire [3:0] bit_extender_1_out, counter_1_q;

  Counter #(.width(4), .max('h8), .ongoal("stay")) counter_1 (
    .Q(counter_1_q), .clk(clock_1_out));  // open: load, D, count, carry, clr
  Clock clock_1 (.out(clock_1_out));
  assign bit_extender_1_out = {{1{1'b0}}, \input };  // Bit_Extender bit_extender_1
  // Probe on counter_1_q
  // Probe on bit_extender_1_out
  Comparator #(.width(4), .mode("unsigned")) comparator_1 (
    .a(bit_extender_1_out), .b(counter_1_q), .lt(out_2));  // open: gt, eq
endmodule

module calculator (
  input  signal,
  output [3:0] now_value
);

  wire clk, \initial , not_1_out;
  wire [3:0] adder_1_out, multiplexer_1_out, pre_q;

  // Probe on now_value
  Counter #(.width(1), .max('h1), .ongoal("stay")) counter_1 (
    .Q(\initial ), .clk(clk));  // open: load, D, count, carry, clr
  Clock clock_1 (.out(clk));
  Multiplexer #(.width(4)) multiplexer_1 (
    .in0(4'b0001), .in1(now_value), .out(multiplexer_1_out), .sel(\initial ));  // open: en
  not not_1 (not_1_out, signal);
  Register #(.width(4)) pre (.D(multiplexer_1_out), .en(not_1_out), .Q(pre_q), .clk(clk));  // open: clr
  Adder #(.width(4)) adder_1 (.a(now_value), .b(pre_q), .out(adder_1_out));  // open: cin, cout
  Register #(.width(4)) now (.D(adder_1_out), .en(not_1_out), .Q(now_value), .clk(clk));  // open: clr
endmodule
