// Logisim project fib_plus.circ as structural Verilog: 6 circuits, main circuit main
module main (
  input  [31:0] N,
  output [31:0] Nth
);

  wire counter_freeze;
  wire [31:0] counter_n_2;

  counter counter (.N(N), .n_2(counter_n_2), .freeze(counter_freeze));
  calculator calculator (.n(counter_n_2), .freeze(counter_freeze), .ans(Nth));
endmodule

// X
module matrix_multiply (
  input  [31:0] A11,
  input  [31:0] A12,
  input  [31:0] A21,
  input  [31:0] A22,
  input  [31:0] B11,
  input  [31:0] B12,
  input  [31:0] B21,
  input  [31:0] B22,
  output [31:0] C11,
  output [31:0] C12,
  output [31:0] C21,
  output [31:0] C22
);

  wire [31:0] multiplier_1_out, multiplier_2_out, multiplier_3_out, multiplier_4_out, multiplier_5_out,
       multiplier_6_out, multiplier_7_out, multiplier_8_out;

  Multiplier #(.width(32)) multiplier_1 (.a(A11), .b(B11), .out(multiplier_1_out));  // open: cin, cout
  Multiplier #(.width(32)) multiplier_2 (.a(A12), .b(B21), .out(multiplier_2_out));  // open: cin, cout
  Multiplier #(.width(32)) multiplier_3 (.a(A11), .b(B12), .out(multiplier_3_out));  // open: cin, cout
  Multiplier #(.width(32)) multiplier_4 (.a(A12), .b(B22), .out(multiplier_4_out));  // open: cin, cout
  Multiplier #(.width(32)) multiplier_5 (.a(A21), .b(B11), .out(multiplier_5_out));  // open: cin, cout
  Multiplier #(.width(32)) multiplier_6 (.a(A22), .b(B21), .out(multiplier_6_out));  // open: cin, cout
  Multiplier #(.width(32)) multiplier_7 (.a(A21), .b(B12), .out(multiplier_7_out));  // open: cin, cout
  Multiplier #(.width(32)) multiplier_8 (.a(A22), .b(B22), .out(multiplier_8_out));  // open: cin, cout
  Adder #(.width(32)) adder_1 (.a(multiplier_1_out), .b(multiplier_2_out), .out(C11));  // open: cin, cout
  Adder #(.width(32)) adder_2 (.a(multiplier_3_out), .b(multiplier_4_out), .out(C12));  // open: cin, cout
  Adder #(.width(32)) adder_3 (.a(multiplier_5_out), .b(multiplier_6_out), .out(C21));  // open: cin, cout
  Adder #(.width(32)) adder_4 (.a(multiplier_7_out), .b(multiplier_8_out), .out(C22));  // open: cin, cout
endmodule

module calculator (
  input  [31:0] n,
  input  freeze,
  output [31:0] ans
);

  wire bit_extender_1_out, clk, en, \initial , not_2_out, sel;
  wire [31:0] A11, A12, A21, A22, A_E_c11, A_E_c12, A_E_c21, A_E_c22, matrix_multiply_1_c11,
       matrix_multiply_1_c12, matrix_multiply_1_c21, matrix_multiply_1_c22, matrix_mux_1_c11,
       matrix_mux_1_c12, matrix_mux_1_c21, matrix_mux_1_c22, matrix_mux_2_c11, matrix_mux_2_c12,
       matrix_mux_2_c21, matrix_mux_2_c22, out_11, out_12, out_21, out_22, \平方_c11 , \平方_c12 , \平方_c21 ,
       \平方_c22 ;

  Clock clock_1 (.out(clk));
  Counter #(.width(1), .max('h1), .ongoal("stay")) counter_1 (
    .Q(\initial ), .clk(clk));  // open: load, D, count, carry, clr
  not not_1 (en, freeze);
  Bit_Extender #(.in_width(32), .out_width(1)) bit_extender_1 (.in(n), .out(bit_extender_1_out));
  and and_1 (sel, bit_extender_1_out, 1'b1);
  matrix_multiply \u_平方  (
    .A11(A11), .A12(A12), .A21(A21), .A22(A22), .B11(A11), .B12(A12), .B21(A21), .B22(A22), .C11(\平方_c11 ),
    .C12(\平方_c12 ), .C21(\平方_c21 ), .C22(\平方_c22 ));
  matrix_mux A_E (
    .A11(32'h1), .A12({32{1'b0}}), .A21({32{1'b0}}), .A22(32'h1), .B11(A11), .B12(A12), .B21(A21), .B22(A22),
    .select(sel), .C11(A_E_c11), .C12(A_E_c12), .C21(A_E_c21), .C22(A_E_c22));
  matrix_mux matrix_mux_1 (
    .A11(32'h1), .A12(32'h1), .A21(32'h1), .A22({32{1'b0}}), .B11(\平方_c11 ), .B12(\平方_c12 ), .B21(\平方_c21 ),
    .B22(\平方_c22 ), .select(\initial ), .C11(matrix_mux_1_c11), .C12(matrix_mux_1_c12),
    .C21(matrix_mux_1_c21), .C22(matrix_mux_1_c22));
  matrix_multiply matrix_multiply_1 (
    .A11(out_11), .A12(out_12), .A21(out_21), .A22(out_22), .B11(A_E_c11), .B12(A_E_c12), .B21(A_E_c21),
    .B22(A_E_c22), .C11(matrix_multiply_1_c11), .C12(matrix_multiply_1_c12), .C21(matrix_multiply_1_c21),
    .C22(matrix_multiply_1_c22));
  matrix_register A (
    .A11_in(matrix_mux_1_c11), .A12_in(matrix_mux_1_c12), .A21_in(matrix_mux_1_c21),
    .A22_in(matrix_mux_1_c22), .en(en), .clk(clk), .A11_out(A11), .A12_out(A12), .A21_out(A21), .A22_out(A22));
  matrix_mux matrix_mux_2 (
    .A11(32'h1), .A12({32{1'b0}}), .A21({32{1'b0}}), .A22(32'h1), .B11(matrix_multiply_1_c11),
    .B12(matrix_multiply_1_c12), .B21(matrix_multiply_1_c21), .B22(matrix_multiply_1_c22),
    .select(\initial ), .C11(matrix_mux_2_c11), .C12(matrix_mux_2_c12), .C21(matrix_mux_2_c21),
    .C22(matrix_mux_2_c22));
  matrix_register res (
    .A11_in(matrix_mux_2_c11), .A12_in(matrix_mux_2_c12), .A21_in(matrix_mux_2_c21),
    .A22_in(matrix_mux_2_c22), .en(en), .clk(clk), .A11_out(out_11), .A12_out(out_12), .A21_out(out_21),
    .A22_out(out_22));
  Multiplexer #(.width(32)) multiplexer_1 (.in0({32{1'b0}}), .in1(out_12), .out(ans), .sel(not_2_out));  // open: en
  not not_2 (not_2_out, en);
endmodule

module matrix_register (
  input  [31:0] A11_in,
  input  [31:0] A12_in,
  input  [31:0] A21_in,
  input  [31:0] A22_in,
  input  en,
  input  clk,
  output [31:0] A11_out,
  output [31:0] A12_out,
  output [31:0] A21_out,
  output [31:0] A22_out
);

  Register #(.width(32)) register_1 (.D(A11_in), .en(en), .Q(A11_out), .clk(clk));  // open: clr
  Register #(.width(32)) register_2 (.D(A12_in), .en(en), .Q(A12_out), .clk(clk));  // open: clr
  Register #(.width(32)) register_3 (.D(A21_in), .en(en), .Q(A21_out), .clk(clk));  // open: clr
  Register #(.width(32)) register_4 (.D(A22_in), .en(en), .Q(A22_out), .clk(clk));  // open: clr
endmodule

// MUX
module matrix_mux (
  input  [31:0] A11,
  input  [31:0] A12,
  input  [31:0] A21,
  input  [31:0] A22,
  input  [31:0] B11,
  input  [31:0] B12,
  input  [31:0] B21,
  input  [31:0] B22,
  input  select,
  output [31:0] C11,
  output [31:0] C12,
  output [31:0] C21,
  output [31:0] C22
);

  Multiplexer #(.width(32)) multiplexer_1 (.in0(A11), .in1(B11), .out(C11), .sel(select));  // open: en
  Multiplexer #(.width(32)) multiplexer_2 (.in0(A12), .in1(B12), .out(C12), .sel(select));  // open: en
  Multiplexer #(.width(32)) multiplexer_3 (.in0(A21), .in1(B21), .out(C21), .sel(select));  // open: en
  Multiplexer #(.width(32)) multiplexer_4 (.in0(A22), .in1(B22), .out(C22), .sel(select));  // open: en
endmodule

module counter (
  input  [31:0] N,
  output [31:0] n_2,
  output freeze
);

  wire clock_1_out, comparator_1_eq, \initial ;
  wire [31:0] multiplexer_2_out, shifter_1_out;

  Counter #(.width(1), .max('h1), .ongoal("stay")) counter_1 (
    .Q(\initial ), .clk(clock_1_out));  // open: load, D, count, carry, clr
  Clock clock_1 (.out(clock_1_out));
  Comparator #(.width(32), .mode("unsigned")) comparator_1 (
    .a(n_2), .b({32{1'b0}}), .eq(comparator_1_eq));  // open: gt, lt
  Shifter #(.width(32), .shift("lr")) shifter_1 (.in(n_2), .\dist (5'b00001), .out(shifter_1_out));
  Multiplexer multiplexer_1 (.in0(1'b0), .in1(comparator_1_eq), .out(freeze), .sel(\initial ));  // open: en
  Multiplexer #(.width(32)) multiplexer_2 (
    .in0(N), .in1(shifter_1_out), .out(multiplexer_2_out), .sel(\initial ));  // open: en
  Register #(.width(32)) register_1 (.D(multiplexer_2_out), .Q(n_2), .clk(clock_1_out));  // open: en, clr

  // Other names for the same wires on the sheet: output[31:0] = n_2
endmodule
