// Logisim project fibonacci.circ as structural Verilog: 5 circuits, main circuit main
module main (
  input  in_1,
  input  [2:0] in_2,
  output [3:0] out_3
);

  wire clock_1_out, comparator_1_gt, not_1_out, timecounting_1_out_2;
  wire [3:0] adder_1_out, n4bit_shifter_1_out_4, register_1_q, register_2_q;

  timecounting timecounting_1 (.in_1(in_2), .out_2(timecounting_1_out_2));
  _4bit_shifter u_4bit_shifter_1 (
    .in_1(4'b0001), .in_2(adder_1_out), .in_3(comparator_1_gt), .out_4(n4bit_shifter_1_out_4));
  not not_1 (not_1_out, timecounting_1_out_2);
  Register #(.width(4)) register_1 (
    .D(register_2_q), .en(timecounting_1_out_2), .Q(register_1_q), .clk(clock_1_out), .clr(in_1));
  Register #(.width(4)) register_2 (
    .D(n4bit_shifter_1_out_4), .en(timecounting_1_out_2), .Q(register_2_q), .clk(clock_1_out), .clr(in_1));
  Clock clock_1 (.out(clock_1_out));
  Comparator #(.width(4), .mode("unsigned")) comparator_1 (
    .a(register_2_q), .b(4'b0000), .gt(comparator_1_gt));  // open: eq, lt
  _4bit_shifter u_4bit_shifter_2 (.in_1(4'b0000), .in_2(register_2_q), .in_3(not_1_out), .out_4(out_3));
  Adder #(.width(4)) adder_1 (.a(register_1_q), .b(register_2_q), .out(adder_1_out));  // open: cin, cout

  // Other names for the same wires on the sheet: i = in_1
endmodule

module timecounting (
  input  [2:0] in_1,
  output out_2
);

  wire clock_1_out, comparator_1_eq;
  wire [2:0] adder_1_out, register_1_q;

  Adder #(.width(3)) adder_1 (.a(3'b001), .b(register_1_q), .out(adder_1_out));  // open: cin, cout
  Register #(.width(3)) register_1 (.D(adder_1_out), .en(out_2), .Q(register_1_q), .clk(clock_1_out));  // open: clr
  Clock clock_1 (.out(clock_1_out));
  Comparator #(.width(3)) comparator_1 (.a(in_1), .b(register_1_q), .eq(comparator_1_eq));  // open: gt, lt
  not not_1 (out_2, comparator_1_eq);
endmodule

module _3bit_shifter (
  input  [2:0] in_1,
  input  [2:0] in_2,
  input  in_3,
  output [2:0] out_4
);

  _1bit_shifter u_1bit_shifter_1 (.a(in_1[0]), .b(in_2[0]), .c(in_3), .a1(out_4[0]));  // open: b1
  _1bit_shifter u_1bit_shifter_2 (.a(in_1[1]), .b(in_2[1]), .c(in_3), .a1(out_4[1]));  // open: b1
  _1bit_shifter u_1bit_shifter_3 (.a(in_1[2]), .b(in_2[2]), .c(in_3), .a1(out_4[2]));  // open: b1
endmodule

module _1bit_shifter (
  input  a,
  input  b,
  input  c,
  output a1,
  output b1
);

  wire and_1_out, and_2_out, and_3_out, and_4_out, not_1_out, not_2_out;

  not not_1 (not_1_out, c);
  not not_2 (not_2_out, c);
  and and_1 (and_1_out, b, c);
  and and_2 (and_2_out, a, not_1_out);
  and and_3 (and_3_out, b, not_2_out);
  and and_4 (and_4_out, a, c);
  or or_1 (a1, and_1_out, and_2_out);
  or or_2 (b1, and_3_out, and_4_out);
endmodule

module _4bit_shifter (
  input  [3:0] in_1,
  input  [3:0] in_2,
  input  in_3,
  output [3:0] out_4
);

  _1bit_shifter u_1bit_shifter_1 (.a(in_1[0]), .b(in_2[0]), .c(in_3), .a1(out_4[0]));  // open: b1
  _1bit_shifter u_1bit_shifter_2 (.a(in_1[1]), .b(in_2[1]), .c(in_3), .a1(out_4[1]));  // open: b1
  _1bit_shifter u_1bit_shifter_3 (.a(in_1[2]), .b(in_2[2]), .c(in_3), .a1(out_4[2]));  // open: b1
  _1bit_shifter u_1bit_shifter_4 (.a(in_1[3]), .b(in_2[3]), .c(in_3), .a1(out_4[3]));  // open: b1
endmodule
