// Logisim project fsm.circ as structural Verilog: 3 circuits, main circuit fsm
module fsm (
  input  [1:0] In,
  input  clr,
  output out_3
);

  wire clock_1_out;
  wire [2:0] multiplexer_1_out, register_1_q, transfer_1_out_3;

  transfer transfer_1 (.I(In), .S(register_1_q), .out_3(transfer_1_out_3));
  Multiplexer #(.width(3)) multiplexer_1 (
    .in0(transfer_1_out_3), .in1(3'b000), .out(multiplexer_1_out), .sel(clr));  // open: en
  Clock clock_1 (.out(clock_1_out));
  Register #(.width(3)) register_1 (.D(multiplexer_1_out), .Q(register_1_q), .clk(clock_1_out));  // open: en, clr
  \output  output_1 (.I(In), .S(register_1_q), .\output (out_3));
endmodule

module transfer (
  input  [1:0] I,
  input  [2:0] S,
  output [2:0] out_3
);

  wire and_2_out, and_3_out, and_4_out, and_5_out, and_6_out, and_7_out, and_8_out, and_9_out, not_1_out,
       not_2_out, not_3_out, not_4_out, not_5_out, not_6_out, not_7_out, not_8_out, not_9_out, not_10_out,
       not_11_out, not_12_out, not_13_out, not_14_out, not_15_out, not_16_out, not_17_out;

  not not_1 (not_1_out, I[0]);
  not not_2 (not_2_out, I[1]);
  not not_3 (not_3_out, S[1]);
  not not_4 (not_4_out, I[0]);
  not not_5 (not_5_out, S[1]);
  not not_6 (not_6_out, I[1]);
  not not_7 (not_7_out, S[0]);
  not not_8 (not_8_out, I[0]);
  not not_9 (not_9_out, S[0]);
  not not_10 (not_10_out, I[0]);
  not not_11 (not_11_out, S[1]);
  not not_12 (not_12_out, I[0]);
  not not_13 (not_13_out, S[0]);
  not not_14 (not_14_out, I[1]);
  not not_15 (not_15_out, S[1]);
  not not_16 (not_16_out, S[0]);
  not not_17 (not_17_out, I[1]);
  and and_1 (out_3[2], not_1_out, S[1], S[0]);
  and and_2 (and_2_out, not_2_out, not_3_out, S[0]);
  and and_3 (and_3_out, not_4_out, not_5_out, S[0]);
  and and_4 (and_4_out, not_6_out, S[1], not_7_out);
  and and_5 (and_5_out, not_8_out, S[1], not_9_out);
  and and_6 (and_6_out, not_10_out, not_11_out, S[0]);
  and and_7 (and_7_out, not_12_out, S[1], not_13_out);
  and and_8 (and_8_out, not_14_out, I[0], not_15_out, not_16_out);
  and and_9 (and_9_out, not_17_out, I[0], S[1], S[0]);
  or or_1 (out_3[1], and_2_out, and_3_out, and_4_out, and_5_out);
  or or_2 (out_3[0], and_6_out, and_7_out, and_8_out, and_9_out);
endmodule

module \output  (
  input  [1:0] I,
  input  [2:0] S,
  output \output 
);

  wire not_1_out;

  not not_1 (not_1_out, I[0]);
  and and_1 (\output , not_1_out, S[1], S[0]);
endmodule
