// Logisim project ftoi.circ as structural Verilog: 2 circuits, main circuit ftoi
module ftoi (
  input  [15:0] float,
  output [31:0] out_2
);

  wire comparator_1_eq, comparator_2_eq, comparator_3_gt, zero_signal;
  wire [4:0] subtractor_1_out;
  wire [31:0] ans, cal_1_out_3, negator_1_out;

  // Probe on subtractor_1_out
  Subtractor #(.width(5)) subtractor_1 (.a(float[14:10]), .b(5'b01111), .out(subtractor_1_out));  // open: bin, bout
  Comparator #(.width(5)) comparator_1 (.a({5{1'b1}}), .b(float[14:10]), .eq(comparator_1_eq));  // open: gt, lt
  Comparator #(.width(5)) comparator_2 (.a(float[14:10]), .b({5{1'b0}}), .eq(comparator_2_eq));  // open: gt, lt
  Comparator #(.width(5)) comparator_3 (.a({5{1'b0}}), .b(subtractor_1_out), .gt(comparator_3_gt));  // open: eq, lt
  or or_1 (zero_signal, comparator_1_eq, comparator_2_eq, comparator_3_gt);
  cal cal_1 (.n(subtractor_1_out), .fra(float[9:0]), .out_3(cal_1_out_3));
  Negator #(.width(32)) negator_1 (.in(cal_1_out_3), .out(negator_1_out));
  Multiplexer #(.width(32)) multiplexer_1 (
    .in0(cal_1_out_3), .in1(negator_1_out), .out(ans), .sel(float[15]));  // open: en
  Multiplexer #(.width(32)) multiplexer_2 (.in0(ans), .in1({32{1'b0}}), .out(out_2), .sel(zero_signal));  // open: en

  // Other names for the same wires on the sheet: fra[9:0] = float[9:0]; exp[4:0] = float[14:10]; sign = float[15]
endmodule

module cal (
  input  [4:0] n,
  input  [9:0] fra,
  output [31:0] out_3
);

  wire and_1_out, and_2_out, and_3_out, and_4_out, and_5_out, and_6_out, and_7_out, and_8_out, and_9_out,
       and_10_out, comparator_1_lt, comparator_2_lt, comparator_3_lt, comparator_4_lt, comparator_5_lt,
       comparator_6_lt, comparator_7_lt, comparator_8_lt, comparator_9_lt, comparator_10_lt, not_1_out,
       not_2_out, not_3_out, not_4_out, not_5_out, not_6_out, not_7_out, not_8_out, not_9_out, not_10_out;
  wire [4:0] subtractor_1_out, subtractor_2_out, subtractor_3_out, subtractor_4_out, subtractor_5_out,
       subtractor_6_out, subtractor_7_out, subtractor_8_out, subtractor_9_out, subtractor_10_out;
  wire [31:0] adder_1_out, adder_2_out, adder_3_out, adder_4_out, adder_5_out, adder_6_out, adder_7_out,
       adder_8_out, adder_9_out, bit_extender_1_out, bit_extender_2_out, bit_extender_3_out,
       bit_extender_4_out, bit_extender_5_out, bit_extender_6_out, bit_extender_7_out, bit_extender_8_out,
       bit_extender_9_out, bit_extender_10_out, multiplier_1_out, multiplier_2_out, multiplier_3_out,
       multiplier_4_out, multiplier_5_out, multiplier_6_out, multiplier_7_out, multiplier_8_out,
       multiplier_9_out, multiplier_10_out, shifter_1_out, shifter_2_out, shifter_3_out, shifter_4_out,
       shifter_5_out, shifter_6_out, shifter_7_out, shifter_8_out, shifter_9_out, shifter_10_out,
       shifter_11_out;

  Subtractor #(.width(5)) subtractor_1 (.a(n), .b(5'b00001), .out(subtractor_1_out));  // open: bin, bout
  Subtractor #(.width(5)) subtractor_2 (.a(n), .b(5'b00010), .out(subtractor_2_out));  // open: bin, bout
  Subtractor #(.width(5)) subtractor_3 (.a(n), .b(5'b00011), .out(subtractor_3_out));  // open: bin, bout
  Subtractor #(.width(5)) subtractor_4 (.a(n), .b(5'b00100), .out(subtractor_4_out));  // open: bin, bout
  Subtractor #(.width(5)) subtractor_5 (.a(n), .b(5'b00101), .out(subtractor_5_out));  // open: bin, bout
  Subtractor #(.width(5)) subtractor_6 (.a(n), .b(5'b00110), .out(subtractor_6_out));  // open: bin, bout
  Subtractor #(.width(5)) subtractor_7 (.a(n), .b(5'b00111), .out(subtractor_7_out));  // open: bin, bout
  Subtractor #(.width(5)) subtractor_8 (.a(n), .b(5'b01000), .out(subtractor_8_out));  // open: bin, bout
  Subtractor #(.width(5)) subtractor_9 (.a(n), .b(5'b01001), .out(subtractor_9_out));  // open: bin, bout
  Subtractor #(.width(5)) subtractor_10 (.a(n), .b(5'b01010), .out(subtractor_10_out));  // open: bin, bout
  Shifter #(.width(32)) shifter_1 (.in(32'h1), .\dist (subtractor_1_out), .out(shifter_1_out));
  Comparator #(.width(5)) comparator_1 (.a(subtractor_1_out), .b({5{1'b0}}), .lt(comparator_1_lt));  // open: gt, eq
  not not_1 (not_1_out, comparator_1_lt);
  Shifter #(.width(32)) shifter_2 (.in(32'h1), .\dist (subtractor_2_out), .out(shifter_2_out));
  Comparator #(.width(5)) comparator_2 (.a(subtractor_2_out), .b({5{1'b0}}), .lt(comparator_2_lt));  // open: gt, eq
  Shifter #(.width(32)) shifter_3 (.in(32'h1), .\dist (subtractor_3_out), .out(shifter_3_out));
  Comparator #(.width(5)) comparator_3 (.a(subtractor_3_out), .b({5{1'b0}}), .lt(comparator_3_lt));  // open: gt, eq
  Shifter #(.width(32)) shifter_4 (.in(32'h1), .\dist (subtractor_4_out), .out(shifter_4_out));
  Comparator #(.width(5)) comparator_4 (.a(subtractor_4_out), .b({5{1'b0}}), .lt(comparator_4_lt));  // open: gt, eq
  Shifter #(.width(32)) shifter_5 (.in(32'h1), .\dist (subtractor_5_out), .out(shifter_5_out));
  Comparator #(.width(5)) comparator_5 (.a(subtractor_5_out), .b({5{1'b0}}), .lt(comparator_5_lt));  // open: gt, eq
  Shifter #(.width(32)) shifter_6 (.in(32'h1), .\dist (subtractor_6_out), .out(shifter_6_out));
  Comparator #(.width(5)) comparator_6 (.a(subtractor_6_out), .b({5{1'b0}}), .lt(comparator_6_lt));  // open: gt, eq
  Shifter #(.width(32)) shifter_7 (.in(32'h1), .\dist (subtractor_7_out), .out(shifter_7_out));
  Comparator #(.width(5)) comparator_7 (.a(subtractor_7_out), .b({5{1'b0}}), .lt(comparator_7_lt));  // open: gt, eq
  Shifter #(.width(32)) shifter_8 (.in(32'h1), .\dist (subtractor_8_out), .out(shifter_8_out));
  Comparator #(.width(5)) comparator_8 (.a(subtractor_8_out), .b({5{1'b0}}), .lt(comparator_8_lt));  // open: gt, eq
  Shifter #(.width(32)) shifter_9 (.in(32'h1), .\dist (subtractor_9_out), .out(shifter_9_out));
  Comparator #(.width(5)) comparator_9 (.a(subtractor_9_out), .b({5{1'b0}}), .lt(comparator_9_lt));  // open: gt, eq
  Shifter #(.width(32)) shifter_10 (.in(32'h1), .\dist (subtractor_10_out), .out(shifter_10_out));
  Comparator #(.width(5)) comparator_10 (.a(subtractor_10_out), .b({5{1'b0}}), .lt(comparator_10_lt));  // open: gt, eq
  not not_2 (not_2_out, comparator_2_lt);
  not not_3 (not_3_out, comparator_3_lt);
  not not_4 (not_4_out, comparator_4_lt);
  not not_5 (not_5_out, comparator_5_lt);
  not not_6 (not_6_out, comparator_6_lt);
  not not_7 (not_7_out, comparator_7_lt);
  not not_8 (not_8_out, comparator_8_lt);
  not not_9 (not_9_out, comparator_9_lt);
  not not_10 (not_10_out, comparator_10_lt);
  and and_1 (and_1_out, not_1_out, fra[9]);
  and and_2 (and_2_out, not_2_out, fra[8]);
  and and_3 (and_3_out, not_3_out, fra[7]);
  and and_4 (and_4_out, not_4_out, fra[6]);
  and and_5 (and_5_out, not_5_out, fra[5]);
  and and_6 (and_6_out, not_6_out, fra[4]);
  and and_7 (and_7_out, not_7_out, fra[3]);
  and and_8 (and_8_out, not_8_out, fra[2]);
  and and_9 (and_9_out, not_9_out, fra[1]);
  and and_10 (and_10_out, not_10_out, fra[0]);
  assign bit_extender_1_out = {{31{1'b0}}, and_1_out};  // Bit_Extender bit_extender_1
  assign bit_extender_2_out = {{31{1'b0}}, and_2_out};  // Bit_Extender bit_extender_2
  assign bit_extender_3_out = {{31{1'b0}}, and_3_out};  // Bit_Extender bit_extender_3
  assign bit_extender_4_out = {{31{1'b0}}, and_4_out};  // Bit_Extender bit_extender_4
  assign bit_extender_5_out = {{31{1'b0}}, and_5_out};  // Bit_Extender bit_extender_5
  assign bit_extender_6_out = {{31{1'b0}}, and_6_out};  // Bit_Extender bit_extender_6
  assign bit_extender_7_out = {{31{1'b0}}, and_7_out};  // Bit_Extender bit_extender_7
  assign bit_extender_8_out = {{31{1'b0}}, and_8_out};  // Bit_Extender bit_extender_8
  assign bit_extender_9_out = {{31{1'b0}}, and_9_out};  // Bit_Extender bit_extender_9
  assign bit_extender_10_out = {{31{1'b0}}, and_10_out};  // Bit_Extender bit_extender_10
  Multiplier #(.width(32)) multiplier_1 (
    .a(shifter_1_out), .b(bit_extender_1_out), .out(multiplier_1_out));  // open: cin, cout
  Multiplier #(.width(32)) multiplier_2 (
    .a(shifter_2_out), .b(bit_extender_2_out), .out(multiplier_2_out));  // open: cin, cout
  Multiplier #(.width(32)) multiplier_3 (
    .a(shifter_3_out), .b(bit_extender_3_out), .out(multiplier_3_out));  // open: cin, cout
  Multiplier #(.width(32)) multiplier_4 (
    .a(shifter_4_out), .b(bit_extender_4_out), .out(multiplier_4_out));  // open: cin, cout
  Multiplier #(.width(32)) multiplier_5 (
    .a(shifter_5_out), .b(bit_extender_5_out), .out(multiplier_5_out));  // open: cin, cout
  Multiplier #(.width(32)) multiplier_6 (
    .a(shifter_6_out), .b(bit_extender_6_out), .out(multiplier_6_out));  // open: cin, cout
  Multiplier #(.width(32)) multiplier_7 (
    .a(shifter_7_out), .b(bit_extender_7_out), .out(multiplier_7_out));  // open: cin, cout
  Multiplier #(.width(32)) multiplier_8 (
    .a(shifter_8_out), .b(bit_extender_8_out), .out(multiplier_8_out));  // open: cin, cout
  Multiplier #(.width(32)) multiplier_9 (
    .a(shifter_9_out), .b(bit_extender_9_out), .out(multiplier_9_out));  // open: cin, cout
  Multiplier #(.width(32)) multiplier_10 (
    .a(shifter_10_out), .b(bit_extender_10_out), .out(multiplier_10_out));  // open: cin, cout
  Adder #(.width(32)) adder_1 (.a(multiplier_1_out), .b(multiplier_2_out), .out(adder_1_out));  // open: cin, cout
  Adder #(.width(32)) adder_2 (.a(multiplier_3_out), .b(multiplier_4_out), .out(adder_2_out));  // open: cin, cout
  Adder #(.width(32)) adder_3 (.a(multiplier_5_out), .b(multiplier_6_out), .out(adder_3_out));  // open: cin, cout
  Adder #(.width(32)) adder_4 (.a(multiplier_7_out), .b(multiplier_8_out), .out(adder_4_out));  // open: cin, cout
  Adder #(.width(32)) adder_5 (.a(multiplier_9_out), .b(multiplier_10_out), .out(adder_5_out));  // open: cin, cout
  Adder #(.width(32)) adder_6 (.a(adder_1_out), .b(adder_2_out), .out(adder_6_out));  // open: cin, cout
  Adder #(.width(32)) adder_7 (.a(adder_3_out), .b(adder_4_out), .out(adder_7_out));  // open: cin, cout
  Adder #(.width(32)) adder_8 (.a(adder_7_out), .b(adder_5_out), .out(adder_8_out));  // open: cin, cout
  Shifter #(.width(32)) shifter_11 (.in(32'h1), .\dist (n), .out(shifter_11_out));
  Adder #(.width(32)) adder_9 (.a(adder_6_out), .b(adder_8_out), .out(adder_9_out));  // open: cin, cout
  Adder #(.width(32)) adder_10 (.a(shifter_11_out), .b(adder_9_out), .out(out_3));  // open: cin, cout

  // Other names for the same wires on the sheet: num10 = fra[0]; num9 = fra[1]; num8 = fra[2]; num7 = fra[3];
  //   num6 = fra[4]; num5 = fra[5]; num4 = fra[6]; num3 = fra[7]; num2 = fra[8]; num1 = fra[9]
endmodule
