// Logisim project referee.circ as structural Verilog: 1 circuit, main circuit main
module main (
  input  A,
  input  B,
  input  C,
  input  in_4,
  output A_2,
  output B_2,
  output C_2
);

  wire clk, d_ff_1_q, d_ff_2_q, d_ff_3_q, not_1_out, not_2_out, not_3_out, not_4_out, not_5_out, not_6_out;

  Clock clock_1 (.out(clk));
  D_Flip_Flop d_ff_1 (.clk(clk), .D(A), .Q(d_ff_1_q), .reset(in_4));  // open: Qn, preset, en
  D_Flip_Flop d_ff_2 (.clk(clk), .D(B), .Q(d_ff_2_q), .reset(in_4));  // open: Qn, preset, en
  D_Flip_Flop d_ff_3 (.clk(clk), .D(C), .Q(d_ff_3_q), .reset(in_4));  // open: Qn, preset, en
  not not_1 (not_1_out, B_2);
  not not_2 (not_2_out, C_2);
  not not_3 (not_3_out, A_2);
  not not_4 (not_4_out, C_2);
  not not_5 (not_5_out, A_2);
  not not_6 (not_6_out, B_2);
  and and_1 (A_2, d_ff_1_q, not_1_out, not_2_out);
  and and_2 (B_2, d_ff_2_q, not_3_out, not_4_out);
  and and_3 (C_2, d_ff_3_q, not_5_out, not_6_out);

  // Other names for the same wires on the sheet: referee = in_4
endmodule
