// Logisim project 三进制.circ as structural Verilog: 1 circuit, main circuit main
module main (
  input  a1,
  input  a0,
  input  b1,
  input  b0,
  output S1,
  output S0,
  output C
);

  wire and_1_out, and_2_out, and_3_out, and_4_out, and_5_out, and_6_out, and_7_out, and_8_out, and_9_out,
       not_1_out, not_2_out, not_3_out, not_4_out;

  not not_1 (not_1_out, b0);
  not not_2 (not_2_out, a1);
  not not_3 (not_3_out, a0);
  not not_4 (not_4_out, b1);
  and and_1 (and_1_out, not_2_out, not_3_out, b1, not_1_out);
  and and_2 (and_2_out, not_2_out, a0, not_4_out, b0);
  and and_3 (and_3_out, a1, not_3_out, not_4_out, not_1_out);
  and and_4 (and_4_out, not_2_out, not_3_out, not_4_out, b0);
  and and_5 (and_5_out, not_2_out, a0, not_4_out, not_1_out);
  and and_6 (and_6_out, a1, not_3_out, b1, not_1_out);
  and and_7 (and_7_out, not_2_out, a0, b1, not_1_out);
  and and_8 (and_8_out, a1, not_3_out, not_4_out, b0);
  and and_9 (and_9_out, a1, not_3_out, b1, not_1_out);
  or or_1 (S1, and_1_out, and_2_out, and_3_out);
  or or_2 (S0, and_4_out, and_5_out, and_6_out);
  or or_3 (C, and_7_out, and_8_out, and_9_out);
endmodule
