// Logisim project CPU.circ as structural Verilog: 8 circuits, main circuit main
module main (
  input  in_1,
  output [31:0] out_2,
  output out_3,
  output [4:0] out_4,
  output [31:0] out_5,
  output out_6,
  output [4:0] out_7,
  output [31:0] out_8
);

  wire Beq_Zero, clk, Controller_alusrc, Controller_extop;
  wire [1:0] Controller_regdst, Controller_wdsel;
  wire [2:0] Controller_aluop, Controller_npcop;
  wire [31:0] adder_1_out, ALU_alu_result, DM_readdata, EXT_extimm, GRF_rd1, IFU_pc, multiplexer_3_out,
       NPC_next_pc;

  Clock clock_1 (.out(clk));
  // Probe on NPC_next_pc
  // Probe on Controller_npcop
  NPC NPC (
    .PC(IFU_pc), .offset(EXT_extimm), .next_PC(NPC_next_pc), .NPCOp(Controller_npcop), .Instr(out_2[25:0]),
    .JumpRegister(GRF_rd1), .zero(Beq_Zero));
  IFU IFU (.clk(clk), .reset(in_1), .next_PC(NPC_next_pc), .Instr(out_2), .PC(IFU_pc));
  // Probe on IFU_pc
  // Probe on out_2
  // Probe on Controller_regdst
  Adder #(.width(32)) adder_1 (.a(IFU_pc), .b(32'h3004), .out(adder_1_out));  // open: cin, cout
  // Probe on Controller_wdsel
  Multiplexer #(.select(2), .width(5)) multiplexer_1 (
    .in0(out_2[20:16]), .in1(out_2[15:11]), .in2({5{1'b1}}), .out(out_4), .sel(Controller_regdst));  // open: in3, en
  Controller Controller (
    .op(out_2[31:26]), .func(out_2[5:0]), .MemWrite(out_6), .ALUOp(Controller_aluop),
    .ALUSrc(Controller_alusrc), .RegWrite(out_3), .ExtOp(Controller_extop), .NPCOp(Controller_npcop),
    .RegDst(Controller_regdst), .WDSel(Controller_wdsel));
  Multiplexer #(.select(2), .width(32)) multiplexer_2 (
    .in0({ALU_alu_result[31:7], out_7, ALU_alu_result[1:0]}), .in1(DM_readdata), .in2(adder_1_out),
    .out(out_5), .sel(Controller_wdsel));  // open: in3, en
  // Probe on out_2[15:0]
  GRF GRF (
    .WD3(out_5), .A3(out_4), .WE3(out_3), .reset(in_1), .clk(clk), .A1(out_2[25:21]), .A2(out_2[20:16]),
    .RD1(GRF_rd1), .RD2(out_8));
  EXT EXT (.Imm(out_2[15:0]), .EXTImm(EXT_extimm), .EXTOp(Controller_extop));
  // Probe on GRF_rd1
  // Probe on EXT_extimm
  Multiplexer #(.width(32)) multiplexer_3 (
    .in0(out_8), .in1(EXT_extimm), .out(multiplexer_3_out), .sel(Controller_alusrc));  // open: en
  // Probe on out_8
  // Probe on Controller_aluop
  ALU ALU (
    .Src_A(GRF_rd1), .Src_B(multiplexer_3_out), .zero(Beq_Zero),
    .ALU_Result({ALU_alu_result[31:7], out_7, ALU_alu_result[1:0]}), .ALUOp(Controller_aluop),
    .in_4(out_2[10:6]));
  // Probe on {ALU_alu_result[31:7], out_7, ALU_alu_result[1:0]}
  DM DM (.WriteData(out_8), .ReadData(DM_readdata), .clk(clk), .reset(in_1), .WE(out_6), .address(out_7));

  // Other names for the same wires on the sheet: MemAddr[4:0] = out_7; Funct[5:0] = out_2[5:0];
  //   Imm16[15:0] = out_2[15:0]; Instr[31:0] = out_2; Instr_Index[25:0] = out_2[25:0]; s[4:0] = out_2[10:6];
  //   Rd[4:0] = out_2[15:11]; Rt[4:0] = out_2[20:16]; Rs[4:0] = out_2[25:21]; Op[5:0] = out_2[31:26];
  //   MemData[31:0] = out_8; MemWrite = out_6; RegAddr[4:0] = out_4; RegData[31:0] = out_5; RegWrite = out_3;
  //   reset = in_1

  // Notes on the sheet:
  //   ALU
  //   DM
  //   PC+4
  //   Rs
  //   Rt
endmodule

module IFU (
  input  clk,
  input  reset,
  input  [31:0] next_PC,
  output [31:0] Instr,
  output [31:0] PC
);

  Register #(.width(32)) u_PC (.D(next_PC), .Q(PC), .clk(clk), .clr(reset));  // open: en
  ROM #(.addrWidth(7), .dataWidth(32)) rom_1 (.addr(PC[8:2]), .data(Instr));  // open: sel

  // Notes on the sheet:
  //   contents of rom_1 (hex, n*v repeats v):
  //   35291111 8000c03 354a1111 356b1111 8000c07 35ad1111 8000c09 358c1111 8000c05 35ce1111 c000c0d
  //   34171111 8000c0f 3e07820 3e00008 37181111 37391111 8000c14 36101010 8000c17 1319fffd 36101111
  //   8000c17 13190002 36521111 8000c1e 36521010 8000c1e 36731010 8000c23 c020 37180111 1319fffb 36731111
  //   8000c23 1319ffff 36941111 8000c26 13190002 36b51111 8000c2b 36b51010 8000c2b 20160001
endmodule

module GRF (
  input  [31:0] WD3,
  input  [4:0] A3,
  input  WE3,
  input  reset,
  input  clk,
  input  [4:0] A1,
  input  [4:0] A2,
  output [31:0] RD1,
  output [31:0] RD2
);

  wire [31:0] _0, _1, _2, _3, _4, _5, _6, _7, _8, _9, _10, _11, _12, _13, _14, _15, _16, _17, _18, _19, _20,
       _21, _22, _23, _24, _25, _26, _27, _28, _29, _30, _31, I1, I2, I3, I4, I5, I6, I7, I8, I9, I10, I11,
       I12, I13, I14, I15, I16, I17, I18, I19, I20, I21, I22, I23, I24, I25, I26, I27, I28, I29, I30, I31;

  Demultiplexer #(.select(5), .width(32), .tristate("true")) demultiplexer_1 (
    .out1(I1), .out2(I2), .out3(I3), .out4(I4), .out5(I5), .out6(I6), .out7(I7), .out8(I8), .out9(I9),
    .out10(I10), .out11(I11), .out12(I12), .out13(I13), .out14(I14), .out15(I15), .out16(I16), .out17(I17),
    .out18(I18), .out19(I19), .out20(I20), .out21(I21), .out22(I22), .out23(I23), .out24(I24), .out25(I25),
    .out26(I26), .out27(I27), .out28(I28), .out29(I29), .out30(I30), .out31(I31), .in(WD3), .sel(A3), .en(WE3));  // open: out0
  Multiplexer #(.select(5), .width(32)) multiplexer_1 (
    .in0(_0), .in1(_1), .in2(_2), .in3(_3), .in4(_4), .in5(_5), .in6(_6), .in7(_7), .in8(_8), .in9(_9),
    .in10(_10), .in11(_11), .in12(_12), .in13(_13), .in14(_14), .in15(_15), .in16(_16), .in17(_17),
    .in18(_18), .in19(_19), .in20(_20), .in21(_21), .in22(_22), .in23(_23), .in24(_24), .in25(_25),
    .in26(_26), .in27(_27), .in28(_28), .in29(_29), .in30(_30), .in31(_31), .out(RD1), .sel(A1));  // open: en
  Register #(.width(32)) register_1 (.D({32{1'b0}}), .en(WE3), .Q(_0), .clk(clk), .clr(reset));
  Register #(.width(32)) register_2 (.D(I8), .en(WE3), .Q(_8), .clk(clk), .clr(reset));
  Register #(.width(32)) register_3 (.D(I16), .en(WE3), .Q(_16), .clk(clk), .clr(reset));
  Register #(.width(32)) register_4 (.D(I24), .en(WE3), .Q(_24), .clk(clk), .clr(reset));
  Multiplexer #(.select(5), .width(32)) multiplexer_2 (
    .in0(_0), .in1(_1), .in2(_2), .in3(_3), .in4(_4), .in5(_5), .in6(_6), .in7(_7), .in8(_8), .in9(_9),
    .in10(_10), .in11(_11), .in12(_12), .in13(_13), .in14(_14), .in15(_15), .in16(_16), .in17(_17),
    .in18(_18), .in19(_19), .in20(_20), .in21(_21), .in22(_22), .in23(_23), .in24(_24), .in25(_25),
    .in26(_26), .in27(_27), .in28(_28), .in29(_29), .in30(_30), .in31(_31), .out(RD2), .sel(A2));  // open: en
  Register #(.width(32)) register_5 (.D(I1), .en(WE3), .Q(_1), .clk(clk), .clr(reset));
  Register #(.width(32)) register_6 (.D(I9), .en(WE3), .Q(_9), .clk(clk), .clr(reset));
  Register #(.width(32)) register_7 (.D(I17), .en(WE3), .Q(_17), .clk(clk), .clr(reset));
  Register #(.width(32)) register_8 (.D(I25), .en(WE3), .Q(_25), .clk(clk), .clr(reset));
  Register #(.width(32)) register_9 (.D(I2), .en(WE3), .Q(_2), .clk(clk), .clr(reset));
  Register #(.width(32)) register_10 (.D(I10), .en(WE3), .Q(_10), .clk(clk), .clr(reset));
  Register #(.width(32)) register_11 (.D(I18), .en(WE3), .Q(_18), .clk(clk), .clr(reset));
  Register #(.width(32)) register_12 (.D(I26), .en(WE3), .Q(_26), .clk(clk), .clr(reset));
  Register #(.width(32)) register_13 (.D(I3), .en(WE3), .Q(_3), .clk(clk), .clr(reset));
  Register #(.width(32)) register_14 (.D(I11), .en(WE3), .Q(_11), .clk(clk), .clr(reset));
  Register #(.width(32)) register_15 (.D(I19), .en(WE3), .Q(_19), .clk(clk), .clr(reset));
  Register #(.width(32)) register_16 (.D(I27), .en(WE3), .Q(_27), .clk(clk), .clr(reset));
  Register #(.width(32)) register_17 (.D(I4), .en(WE3), .Q(_4), .clk(clk), .clr(reset));
  Register #(.width(32)) register_18 (.D(I12), .en(WE3), .Q(_12), .clk(clk), .clr(reset));
  Register #(.width(32)) register_19 (.D(I20), .en(WE3), .Q(_20), .clk(clk), .clr(reset));
  Register #(.width(32)) register_20 (.D(I28), .en(WE3), .Q(_28), .clk(clk), .clr(reset));
  Register #(.width(32)) register_21 (.D(I5), .en(WE3), .Q(_5), .clk(clk), .clr(reset));
  Register #(.width(32)) register_22 (.D(I13), .en(WE3), .Q(_13), .clk(clk), .clr(reset));
  Register #(.width(32)) register_23 (.D(I21), .en(WE3), .Q(_21), .clk(clk), .clr(reset));
  Register #(.width(32)) register_24 (.D(I29), .en(WE3), .Q(_29), .clk(clk), .clr(reset));
  Register #(.width(32)) register_25 (.D(I6), .en(WE3), .Q(_6), .clk(clk), .clr(reset));
  Register #(.width(32)) register_26 (.D(I14), .en(WE3), .Q(_14), .clk(clk), .clr(reset));
  Register #(.width(32)) register_27 (.D(I22), .en(WE3), .Q(_22), .clk(clk), .clr(reset));
  Register #(.width(32)) register_28 (.D(I30), .en(WE3), .Q(_30), .clk(clk), .clr(reset));
  Register #(.width(32)) register_29 (.D(I7), .en(WE3), .Q(_7), .clk(clk), .clr(reset));
  Register #(.width(32)) register_30 (.D(I15), .en(WE3), .Q(_15), .clk(clk), .clr(reset));
  Register #(.width(32)) register_31 (.D(I23), .en(WE3), .Q(_23), .clk(clk), .clr(reset));
  Register #(.width(32)) register_32 (.D(I31), .en(WE3), .Q(_31), .clk(clk), .clr(reset));
endmodule

module ALU (
  input  [2:0] ALUOp,
  input  [31:0] Src_A,
  input  [31:0] Src_B,
  input  [4:0] in_4,
  output zero,
  output [31:0] ALU_Result
);

  wire [31:0] add, \or , sll, sub;

  Adder #(.width(32)) adder_1 (.a(Src_A), .b(Src_B), .out(add));  // open: cin, cout
  Subtractor #(.width(32)) subtractor_1 (.a(Src_A), .b(Src_B), .out(sub));  // open: bin, bout
  assign \or  = Src_A | Src_B;  // OR_Gate or_1, 32 bits wide
  Shifter #(.width(32)) shifter_1 (.in(Src_B), .\dist (in_4), .out(sll));
  Comparator #(.width(32), .mode("unsigned")) comparator_1 (.a(sub), .b({32{1'b0}}), .eq(zero));  // open: gt, lt
  Multiplexer #(.select(3), .width(32)) multiplexer_1 (
    .in0(add), .in1(sub), .in2(\or ), .in3({Src_B[15:0], {16{1'b0}}}), .in4(sll), .out(ALU_Result),
    .sel(ALUOp));  // open: in5, in6, in7, en

  // Other names for the same wires on the sheet: A[31:0] = Src_A; B[31:0] = Src_B; lui[31:16] = Src_B[15:0];
  //   s[4:0] = in_4
endmodule

module DM (
  input  [4:0] address,
  input  clk,
  input  WE,
  input  reset,
  input  [31:0] WriteData,
  output [31:0] ReadData
);

  RAM #(.addrWidth(5), .dataWidth(32), .bus("separate")) ram_1 (
    .addr(address), .din(WriteData), .data(ReadData), .str(WE), .clk(clk), .clr(reset));  // open: sel, ld
endmodule

module Controller (
  input  [5:0] op,
  input  [5:0] func,
  output MemWrite,
  output ALUSrc,
  output RegWrite,
  output ExtOp,
  output [1:0] RegDst,
  output [1:0] WDSel,
  output [2:0] ALUOp,
  output [2:0] NPCOp
);

  wire add, beq, j, jr, lui, not_1_out, not_2_out, not_3_out, not_4_out, not_5_out, not_6_out, not_7_out,
       not_8_out, not_9_out, not_10_out, not_11_out, not_12_out, ori, sll, sub, sw;

  not not_1 (not_1_out, op[5]);
  not not_2 (not_2_out, op[4]);
  not not_3 (not_3_out, op[3]);
  not not_4 (not_4_out, op[2]);
  not not_5 (not_5_out, op[1]);
  not not_6 (not_6_out, op[0]);
  not not_7 (not_7_out, func[5]);
  not not_8 (not_8_out, func[4]);
  not not_9 (not_9_out, func[3]);
  not not_10 (not_10_out, func[2]);
  not not_11 (not_11_out, func[1]);
  not not_12 (not_12_out, func[0]);
  and u_add (add, not_1_out, not_2_out, not_3_out, not_4_out, not_5_out, not_6_out, func[5], not_8_out, not_9_out, not_10_out, not_11_out, not_12_out);
  and u_sub (sub, not_1_out, not_2_out, not_3_out, not_4_out, not_5_out, not_6_out, func[5], not_8_out, not_9_out, not_10_out, func[1], not_12_out);
  and lw (WDSel[0], op[5], not_2_out, not_3_out, not_4_out, op[1], op[0]);
  and u_sw (sw, op[5], not_2_out, op[3], not_4_out, op[1], op[0]);
  and u_ori (ori, not_1_out, not_2_out, op[3], op[2], not_5_out, op[0]);
  and u_lui (lui, not_1_out, not_2_out, op[3], op[2], op[1], op[0]);
  and u_beq (beq, not_1_out, not_2_out, not_3_out, op[2], not_5_out, not_6_out);
  and u_j (j, not_1_out, not_2_out, not_3_out, not_4_out, op[1], not_6_out);
  and jal (WDSel[1], not_1_out, not_2_out, not_3_out, not_4_out, op[1], op[0]);
  and u_jr (jr, not_1_out, not_2_out, not_3_out, not_4_out, not_5_out, not_6_out, not_7_out, not_8_out, func[3], not_10_out, not_11_out, not_12_out);
  and u_sll (sll, not_1_out, not_2_out, not_3_out, not_4_out, not_5_out, not_6_out, not_7_out, not_8_out, not_9_out, not_10_out, not_11_out, not_12_out);
  buf u_MemWrite (MemWrite, sw);  // OR_Gate
  or or_1 (NPCOp[0], beq, jr);
  or or_2 (NPCOp[1], j, WDSel[1], jr);
  buf ALUOp2 (ALUOp[2], sll);  // OR_Gate
  or ALUOp1 (ALUOp[1], ori, lui);
  or ALUOp0 (ALUOp[0], sub, lui, beq);
  or u_ALUSrc (ALUSrc, WDSel[0], sw, ori, lui);
  buf RegDst1 (RegDst[1], WDSel[1]);  // OR_Gate
  or RegDst0 (RegDst[0], add, sub, sll);
  or u_RegWrite (RegWrite, add, sub, WDSel[0], ori, lui, WDSel[1], sll);
  or u_ExtOp (ExtOp, WDSel[0], sw, beq);

  assign NPCOp[2] = 1'b0;

  // Other names for the same wires on the sheet: lw = WDSel[0]; jal = WDSel[1]

  // Notes on the sheet:
  //   需要进行立即数操作的
endmodule

module EXT (
  input  EXTOp,
  input  [15:0] Imm,
  output [31:0] EXTImm
);

  wire [31:0] bit_extender_1_out, bit_extender_2_out;

  assign bit_extender_1_out = {{16{1'b0}}, Imm};  // Bit_Extender bit_extender_1
  assign bit_extender_2_out = {{16{Imm[15]}}, Imm};  // Bit_Extender bit_extender_2
  Multiplexer #(.width(32)) multiplexer_1 (
    .in0(bit_extender_1_out), .in1(bit_extender_2_out), .out(EXTImm), .sel(EXTOp));  // open: en
endmodule

module NPC (
  input  zero,
  input  [2:0] NPCOp,
  input  [31:0] PC,
  input  [31:0] offset,
  input  [25:0] Instr,
  input  [31:0] JumpRegister,
  output [31:0] next_PC
);

  wire [27:0] subtractor_2_out;
  wire [31:0] adder_1_out, adder_2_out, multiplexer_1_out, shifter_1_out, subtractor_1_out;

  // Probe on Instr
  // Probe on PC
  Shifter #(.width(32)) shifter_1 (.in(offset), .\dist (5'b00010), .out(shifter_1_out));
  Subtractor #(.width(32)) subtractor_1 (.a(JumpRegister), .b(32'h3000), .out(subtractor_1_out));  // open: bin, bout
  Adder #(.width(32)) adder_1 (.a(PC), .b(32'h4), .out(adder_1_out));  // open: cin, cout
  Subtractor #(.width(28)) subtractor_2 (.a({Instr, 2'b00}), .b(28'h3000), .out(subtractor_2_out));  // open: bin, bout
  Adder #(.width(32)) adder_2 (.a(adder_1_out), .b(shifter_1_out), .out(adder_2_out));  // open: cin, cout
  Multiplexer #(.width(32)) multiplexer_1 (
    .in0(adder_1_out), .in1(adder_2_out), .out(multiplexer_1_out), .sel(zero));  // open: en
  Multiplexer #(.select(3), .width(32)) multiplexer_2 (
    .in0(adder_1_out), .in1(multiplexer_1_out), .in2({PC[31:28], subtractor_2_out}), .in3(subtractor_1_out),
    .out(next_PC), .sel(NPCOp));  // open: in4, in5, in6, in7, en

  // Other names for the same wires on the sheet: PC31_28[3:0] = PC[31:28]

  // Notes on the sheet:
  //   j/jal
  //   PC+4
  //   jr
endmodule
